// Logisim project lab1.circ as structural Verilog: 1 circuit, main circuit main
module main (
  input  A,
  input  B,
  input  C,
  output Y
);

  wire or_1_out;

  or or_1 (or_1_out, A, C);
  and and_1 (Y, or_1_out, B);
endmodule
